// Logisim project Group_6.circ as structural Verilog: 5 circuits, main circuit main
module main (
  input  Sign_A,
  input  [11:0] A,
  input  Sign_B,
  input  [11:0] B,
  output Sign,
  output [11:0] A_B,
  output Carry_Out
);

  Significant_adder significant_adder_1 (
    .Sign_A(Sign_A), .Significant_A(A), .Sign_B(Sign_B), .Significant_B(B), .Sign(Sign), .A_B(A_B),
    .Carry(Carry_Out));
endmodule

module Adder (
  input  Sign_A,
  input  [11:0] A___A______B,
  input  Sign_B,
  input  [11:0] B,
  output Sign_Out,
  output [11:0] A_B,
  output Carry_Out
);

  wire [11:0] adder_1_out, n2s_complement_1__2s_comp, n2s_complement_2__2s_comp;

  _2s_complement u_2s_complement_1 (.Input(A___A______B), .Control(Sign_A), ._2s_comp(n2s_complement_1__2s_comp));
  _2s_complement u_2s_complement_2 (.Input(B), .Control(Sign_B), ._2s_comp(n2s_complement_2__2s_comp));
  Adder_part #(.width(12)) adder_1 (
    .a(n2s_complement_1__2s_comp), .b(n2s_complement_2__2s_comp), .out(adder_1_out), .cout(Carry_Out));  // open: cin
  _2s_complement u_2s_complement_3 (.Input(adder_1_out), .Control(Sign_A), ._2s_comp(A_B));

  assign Sign_Out = Sign_A;
endmodule

module Significant_adder (
  input  Sign_A,
  input  [11:0] Significant_A,
  input  Sign_B,
  input  [11:0] Significant_B,
  output Sign,
  output [11:0] A_B,
  output Carry
);

  wire magnitude_comparator_1_sign_a_2, magnitude_comparator_1_sign_b_2;
  wire [11:0] magnitude_comparator_1_a___a____b, magnitude_comparator_1_b;

  Magnitude_Comparator magnitude_comparator_1 (
    .Sign_A(Sign_A), .Significant_A(Significant_A), .Sign_B(Sign_B), .Significant_B(Significant_B),
    .Sign_A_2(magnitude_comparator_1_sign_a_2), .A___A____B(magnitude_comparator_1_a___a____b),
    .Sign_B_2(magnitude_comparator_1_sign_b_2), .B(magnitude_comparator_1_b));
  Adder adder_1 (
    .A___A______B(magnitude_comparator_1_a___a____b), .B(magnitude_comparator_1_b),
    .Sign_A(magnitude_comparator_1_sign_a_2), .Sign_B(magnitude_comparator_1_sign_b_2), .Sign_Out(Sign),
    .A_B(A_B), .Carry_Out(Carry));
endmodule

module _2s_complement (
  input  Control,
  input  [11:0] Input,
  output [11:0] _2s_comp
);

  wire [11:0] xor_1_out;

  assign xor_1_out = {12{Control}} ^ Input;  // XOR_Gate xor_1, 12 bits wide
  Adder_part #(.width(12)) adder_1 (.a({12{1'b0}}), .b(xor_1_out), .out(_2s_comp), .cin(Control));  // open: cout
endmodule

module Magnitude_Comparator (
  input  Sign_A,
  input  [11:0] Significant_A,
  input  Sign_B,
  input  [11:0] Significant_B,
  output Sign_A_2,
  output [11:0] A___A____B,
  output Sign_B_2,
  output [11:0] B
);

  wire comparator_1_lt, not_1_out;

  Comparator #(.width(12), .mode("unsigned")) comparator_1 (
    .a(Significant_A), .b(Significant_B), .lt(comparator_1_lt));  // open: gt, eq
  not not_1 (not_1_out, comparator_1_lt);
  Multiplexer multiplexer_1 (.in0(Sign_A), .in1(Sign_B), .out(Sign_A_2), .sel(comparator_1_lt));  // open: en
  Multiplexer #(.width(12)) multiplexer_2 (
    .in0(Significant_A), .in1(Significant_B), .out(A___A____B), .sel(comparator_1_lt));  // open: en
  Multiplexer multiplexer_3 (.in0(Sign_A), .in1(Sign_B), .out(Sign_B_2), .sel(not_1_out));  // open: en
  Multiplexer #(.width(12)) multiplexer_4 (
    .in0(Significant_A), .in1(Significant_B), .out(B), .sel(not_1_out));  // open: en
endmodule
